# Fritzing sketch AutomotiveFilter (saved by Fritzing 0.9.2b)
circuit board: 8.2cm x 6.3cm
breadboards: 1

parts:
  Fuse = Fuse with Handler [part_number=Htc-15m]
  PowerIn = Power plug
  2000uF = Electrolytic Capacitor [package="100 mil [THT, electrolytic]"]
  10W1 = 1 Ω Resistor [package=THT]
  PowerOut = Power plug
  D3A = Rectifier Diode [part_number=1N540x package="300 mil [THT]"]

nets:
  N1: Fuse.Connector1, PowerIn.VCC
  N2: Fuse.Connector2, D3A.anode
  GND: PowerIn.GND, PowerOut.GND
  N3: 2000uF.-, PowerOut.VCC
  N4: 2000uF.+, 10W1.Pin_1
  N5: 10W1.Pin_0, D3A.cathode

notes:
  IN
  OUT
  AutomotiveFilter by PAKOZM

custom parts:
  Electrolytic Capacitor: Big electrolytic capacitor
  1 Ω Resistor: 10W resistor
  Rectifier Diode: A standard rectifier diode
