# Fritzing sketch AutomotivePowerFilter (saved by Fritzing 0.9.2b)
circuit board: 8.2cm x 6cm
breadboards: 1

parts:
  Fuse1 = Fuse with Handler [part_number=Htc-15m]
  PowerIn = Power plug
  D1 = Rectifier Diode [part_number=1N540x package="300 mil [THT]"]
  2000uF = Electrolytic Capacitor [package="100 mil [THT, electrolytic]"]
  10W1 = 1 Ω Resistor [package=THT]
  PowerOut = Power plug

nets:
  N1: Fuse1.Connector1, PowerIn.VCC
  N2: Fuse1.Connector2, D1.anode
  GND: PowerIn.GND, PowerOut.GND
  N3: D1.cathode, 10W1.Pin_0
  N4: 2000uF.-, PowerOut.VCC
  N5: 2000uF.+, 10W1.Pin_1

notes:
  IN
  OUT
  AutomotiveFilter by PAKOZM

custom parts:
  Electrolytic Capacitor: Big electrolytic capacitor
  1 Ω Resistor: 10W resistor
