# Fritzing sketch EcoDuino (saved by Fritzing 0.9.0b)
circuit board: 6.88566cm x 5.36311cm
breadboards: 1

parts:
  J11 = rounded female pin header, 8 pins [form="♀ (female rounded)"]
  J12 = rounded female pin header, 6 pins [form="♀ (female rounded)"]
  J13 = rounded female pin header, 8 pins [form="♀ (female rounded)"]
  ATMEGA328P = atmega328 [package=dip]
  10uF = Electrolytic Capacitor [capacitance=10µF package="100 mil [THT, electrolytic]"]
  BAT = Battery
  XTAL = Crystal [frequency="16 Mhz" package=THT]
  22pF = Capacitor [package=cap-pth-small2]
  22pF_2 = Capacitor [package=cap-pth-small2]
  10k = Resistor [tolerance=±5% resistance=10k package=THT]
  RST1 = Pushbutton [package="[THT]"]
  LED1 = LED - 5mm [color="Red (633nm)" package="5 mm [THT]"]
  1k = Resistor [tolerance=±5% resistance=1k package=THT]
  REG = Voltage Regulator [package=to220-igo]
  10uF_2 = Electrolytic Capacitor [capacitance=10µF package="100 mil [THT, electrolytic]"]
  S = Toggle Switch [package=THT]
  D1 = Diode [package=diode-1n4001]
  J10 = rounded female pin header, 10 pins [form="♀ (female rounded)"]
  J14 = male pin header, 6 pins [form="♂ (male)"]
  100nF = Ceramic Capacitor [capacitance=100nF package="100 mil [THT, multilayer]"]
  Plug = Power plug
  USB = USB_AB [package=usb-ab-micro-smd]
  ISP = double row male pin header, 6 pins [form="♂ (male)"]

nets:
  D7: J11.pin1, ATMEGA328P.D7
  D6: J11.pin2, ATMEGA328P.D6_(PWM)
  D5: J11.pin3, ATMEGA328P.D5_(PWM)
  D4: J11.pin4, ATMEGA328P.D4
  D3: J11.pin5, ATMEGA328P.D3_(PWM)
  D2: J11.pin6, ATMEGA328P.D2
  D1: J11.pin7, ATMEGA328P.D1_(TX), J14.pin2
  D0: J11.pin8, ATMEGA328P.D0_(RX), J14.pin3
  A0: J12.pin1, ATMEGA328P.A0
  A1: J12.pin2, ATMEGA328P.A1
  A2: J12.pin3, ATMEGA328P.A2
  A3: J12.pin4, ATMEGA328P.A3
  A4: J12.pin5, ATMEGA328P.A4, J10.pin2
  A5: J12.pin6, ATMEGA328P.A5, J10.pin1
  RESET: J13.pin3, ATMEGA328P.RESET, 10k.Pin_1, RST1.Pin_3, RST1.Pin_4, 100nF.0, ISP.pin3
  5V/AVCC/VCC: J13.pin5, ATMEGA328P.VCC, ATMEGA328P.AVCC, 10uF.+, 10k.Pin_0, S.COM, J14.pin4, ISP.pin6
  GND: J13.pin6, J13.pin7, ATMEGA328P.GND, 10uF.-, BAT.-, 22pF.1, 22pF_2.2, RST1.Pin_1, RST1.Pin_2, LED1.cathode, REG.GND, 10uF_2.-, J10.pin4, J14.pin6, Plug.GND, USB.GND, ISP.pin4
  N1: J13.pin8, BAT.+, D1.A, Plug.VCC
  N2: ATMEGA328P.XLAT1, XTAL.pin_0, 22pF_2.1
  N3: ATMEGA328P.XLAT2, XTAL.pin_1, 22pF.2
  D8: ATMEGA328P.D8, J10.pin10
  D9: ATMEGA328P.D9_(PWM), J10.pin9
  D10: ATMEGA328P.D10_(PWM), J10.pin8
  D11: ATMEGA328P.D11_(PWM), J10.pin7, ISP.pin5
  D12: ATMEGA328P.D12, J10.pin6, ISP.pin1
  D13: ATMEGA328P.D13, 1k.Pin_1, J10.pin5, ISP.pin2
  AEREF pin: ATMEGA328P.AREF, J10.pin3
  N4: LED1.anode, 1k.Pin_0
  N5: REG.IN, 10uF_2.+, D1.C
  N6: REG.OUT, S.L2
  USB 5V: S.L1, USB.VBUS
  N7: J14.pin1, 100nF.1

notes:
  2016 v0.1
  by PAKOZM
  ALARDUINO
  2016 v0.3
  ECODUINO
  5V
  GND
  AREF
  7
  8
  ~9
  ~10
  ~6
  ~5
  4
  ~3
  2
  TX->1
  RX<-0
  ~11
  12
  13
  A4
  A3
  A2
  A0
  A1
  A5
  Vcc
  EcoDuino, Arduino with switchable voltage regulator., 0.3
  UART
  gnd
  3v
  5v
  rx
  tx
  rst
  Vin
  Rst
  Reg
  USB
  ISP
  .
  :SCL
  :SDA
  SDA
  SCL
