# Fritzing sketch Remote (saved by Fritzing 0.9.2b)
circuit board: 6cm x 3.1cm
breadboards: 1

parts:
  10k = Resistor [tolerance=±5% resistance=10k package=THT]
  LED = LED - 3mm [color="Red (633nm)" package="3 mm [THT]"]
  MCU = attiny85 [package=dip]
  100nF = Ceramic Capacitor [capacitance=100nF package="100 mil [THT, multilayer]"]
  PINs1 = male pin header, 3 pins [form="♂ (male)"]
  PINs2 = male pin header, 3 pins [form="♂ (male)"]
  1K = Resistor [tolerance=±5% resistance=1k package=THT]
  BTN = Pushbutton [package="[THT]"]
  PRG = Pushbutton [package="[THT]"]
  TX = male pin header, 3 pins [form="♂ (male)"]
  3V = Battery
  10k_2 = Resistor [tolerance=±5% resistance=10k package=THT]
  D1 = Rectifier Diode [part_number=1N4001 package="300 mil [THT]"]

nets:
  N1: 10k.Pin_0, MCU.Pin_1, PINs1.pin1, BTN.Pin_3, BTN.Pin_4
  3V: 10k.Pin_1, MCU.Pin_8, 100nF.0, PRG.Pin_1, PRG.Pin_2, TX.pin2, D1.cathode
  GND: LED.cathode, MCU.Pin_4, 100nF.1, BTN.Pin_1, BTN.Pin_2, TX.pin1, 3V.-, 10k_2.Pin_1
  N2: LED.anode, 1K.Pin_1
  N3: MCU.Pin_2, PINs1.pin2, TX.pin3
  N4: MCU.Pin_3, PINs1.pin3, 1K.Pin_0
  N5: MCU.Pin_5, PINs2.pin1
  N6: MCU.Pin_6, PINs2.pin2
  N7: MCU.Pin_7, PINs2.pin3, PRG.Pin_3, PRG.Pin_4, 10k_2.Pin_0
  N8: 3V.+, D1.anode

notes:
  3:LED
  5:MOSI
  6:MISO
  2:TX
  1:RST
  Vcc
  GND
  7:SCK
  REMOTE V0.1
  PAKOZM (2016)
  +
  -
  CR2032
  data
  VCC
  Remote, Remote control with 433MHz TX, 0.1
  This circuit fits into a wireless doorbell transmiter.
  7:PRG
