# Fritzing sketch Remote_1 (saved by Fritzing 0.9.0b)
circuit board: 4.7cm x 3.2cm
breadboards: 1

parts:
  10k = Resistor [tolerance=±5% resistance=10k package=THT]
  MCU = attiny85 [package=dip]
  100nF = Ceramic Capacitor [capacitance=100nF package="100 mil [THT, multilayer]"]
  PRG = Pushbutton [package="[THT]"]
  10k_2 = Resistor [tolerance=±5% resistance=10k package=THT]
  TX = male pin header, 3 pins [form="♂ (male)"]
  CR2032 = CR2032
  LED = LED - 3mm [color="Red (633nm)" package="3 mm [THT]"]
  BTN = Pushbutton [package="[THT]"]
  1K = Resistor [tolerance=±5% resistance=1k package=THT]

nets:
  N1: 10k.Pin_0, MCU.Pin_1, BTN.Pin_3, BTN.Pin_4
  3V: 10k.Pin_1, MCU.Pin_8, 100nF.0, PRG.Pin_1, PRG.Pin_2, TX.pin2, CR2032.+
  N2: MCU.Pin_2, TX.pin3
  N3: MCU.Pin_3, 1K.Pin_0
  GND: MCU.Pin_4, 100nF.1, 10k_2.Pin_1, TX.pin1, CR2032.-, LED.cathode, BTN.Pin_1, BTN.Pin_2
  N4: MCU.Pin_7, PRG.Pin_3, PRG.Pin_4, 10k_2.Pin_0
  N5: LED.anode, 1K.Pin_1

notes:
  Remote, Remote control with 433MHz TX, 1.0
  CR2032
  .
  REMOTE V1.0
  PAKOZM (2016)
  dat
  Use BTN for data transmision
  Push and mantain PRG button
  while pushing BTN button to start
  programming mode.
  During programming, push several
  times PRG to generate random key.

custom parts:
  CR2032: CR2032 coin cell PCB adapter
